// Logisim project PL Processor.circ as structural Verilog: 28 circuits, main circuit Data Path
module Data_Path (
);

  wire ALU_Ctrl_slt_unsigned, ALU_lessthan, ALU_zero, C2___C3_2_alusrc, C2___C3_2_beq, C2___C3_2_bge,
       C2___C3_2_blt, C2___C3_2_bne, C2___C3_2_memr, C2___C3_2_regw, C2___C3_2_sltu, C3___C4_2_memr,
       C3___C4_2_memw, C3___C4_2_regw, C3___C4_2_wbdata, C4___C5_2_regw, forward_stall_1_stall, Jump,
       Main_Ctrl_alusrc, Main_Ctrl_beq, Main_Ctrl_bge, Main_Ctrl_blt, Main_Ctrl_bne, Main_Ctrl_ext,
       Main_Ctrl_imm11, Main_Ctrl_linkreg, Main_Ctrl_memr, Main_Ctrl_memw, Main_Ctrl_regw, Main_Ctrl_wbdata,
       Master_out, not_1_out, PC_Ctrl_k1cs, PC_Ctrl_k2cs;
  wire [1:0] ALU_Ctrl_pass_by, C2___C3_2_pass_by, forward_stall_1_forwarda, forward_stall_1_forwardb, ID_fun,
       Main_Ctrl_regdst, PCSrc;
  wire [2:0] C2___C3_rd_q, C3___C4_rd_q, C4___C5_rd_q, ID_rd, ID_rs, ID_rt, multiplexer_1_out;
  wire [3:0] ALU_Ctrl_aluop, C2___C3_2_aluop, C2___C3_2_encoded_controls_q;
  wire [4:0] ID_imm5, ID_opcode;
  wire [10:0] ID_imm11;
  wire [15:0] _5_bit_Ext_imm16, adder_2_out, ALU_r, Bubble_2_controls, Bubble_instruction, C1___C2_inst_q,
       C1___C2_pc_1_q, C1___C2_pc_q, C2___C3__5imm_q, C2___C3_a_q, C2___C3_b_q, C2___C3_bta_q, C2___C3_lui_q,
       C2___C3_pc_1_q, C3___C4_b_q, C3___C4_r_q, C4___C5_r_q, Controls_Encoder_encoded_controls, DM_dout,
       IM_inst, LUI__11_shifted_16, multiplexer_2_out, multiplexer_3_out, multiplexer_4_out,
       multiplexer_5_out, multiplexer_6_out, PC_1, PC_Offset_imm5_11, PC_Offset_pc_ra, PC_q, RegFile_busa,
       RegFile_busb, RegFile_r0o, RegFile_r1o, RegFile_r2o, RegFile_r3o, RegFile_r4o, RegFile_r5o,
       RegFile_r6o, RegFile_r7o;

  Register #(.width(16)) PC (.D(multiplexer_2_out), .en(not_1_out), .Q(PC_q), .clk(Master_out));  // open: clr
  Clock Master (.out(Master_out));
  Adder #(.width(16)) adder_1 (.a(16'h1), .b(PC_q), .out(PC_1));  // open: cin, cout
  Instsruction_Memory IM (.ADD(PC_q), .clk(Master_out), .Inst(IM_inst), .Enable(not_1_out));
  Bubble_Inst Bubble (.K1Cs(PC_Ctrl_k1cs), .Valid_nstruction(IM_inst), .Instruction(Bubble_instruction));
  IF_Pipe C1___C2 (
    .PC_1_D(PC_1), .Inst_D(Bubble_instruction), .PC_1_Q(C1___C2_pc_1_q), .Inst_Q(C1___C2_inst_q),
    .Clk(Master_out), .PC_D(PC_q), .PC_Q(C1___C2_pc_q));
  Instsruction_Decoder ID (
    .Instruction(C1___C2_inst_q), .OPCode(ID_opcode), .FUN(ID_fun), .imm5(ID_imm5), .imm11(ID_imm11),
    .Rd(ID_rd), .Rt(ID_rt), .Rs(ID_rs));
  // Probe on RegFile_r0o
  PC_Next PC_Offset (
    .imm5(ID_imm5), .imm11(ID_imm11), .Imm5_11(PC_Offset_imm5_11), .Imm_Type(Main_Ctrl_imm11),
    .PC(C1___C2_pc_q), .Ra(RegFile_busa), .LinkReg(Main_Ctrl_linkreg), .PC_Ra(PC_Offset_pc_ra));
  Load_Upper_Imm LUI (._11_bit_Imm(ID_imm11), ._11_shifted_16(LUI__11_shifted_16));
  Multiplexer #(.select(2), .width(3), .disabled(0), .enable("false")) multiplexer_1 (
    .in0(ID_rt), .in1(ID_rd), .in2(3'b001), .in3(3'b111), .out(multiplexer_1_out), .sel(Main_Ctrl_regdst));
  // Probe on RegFile_r1o
  Multiplexer #(.select(2), .width(16), .disabled(0), .enable("false")) multiplexer_2 (
    .in0(PC_1), .in1(adder_2_out), .in2(C2___C3_bta_q), .out(multiplexer_2_out), .sel(PCSrc));  // open: in3
  Adder #(.width(16)) adder_2 (.a(PC_Offset_imm5_11), .b(PC_Offset_pc_ra), .out(adder_2_out));  // open: cin, cout
  _5_bit_Extender _5_bit_Ext (.Sign(Main_Ctrl_ext), .imm6(ID_imm5), .imm16(_5_bit_Ext_imm16));
  ALU_Ctrl ALU_Ctrl (
    .FUN(ID_fun), .OP(ID_opcode), .ALUOP(ALU_Ctrl_aluop), .SLT_Unsigned(ALU_Ctrl_slt_unsigned),
    .Pass_By(ALU_Ctrl_pass_by));
  Main_Ctrl Main_Ctrl (
    .OP(ID_opcode), .RegDst(Main_Ctrl_regdst), .WBData(Main_Ctrl_wbdata), .Ext(Main_Ctrl_ext),
    .MEMW(Main_Ctrl_memw), .ALUSRC(Main_Ctrl_alusrc), .RegW(Main_Ctrl_regw), .Imm11(Main_Ctrl_imm11),
    .LinkReg(Main_Ctrl_linkreg), .BEQ(Main_Ctrl_beq), .BNE(Main_Ctrl_bne), .BLT(Main_Ctrl_blt),
    .BGE(Main_Ctrl_bge), .Jump(Jump), .MEMR(Main_Ctrl_memr));
  // Probe on RegFile_r3o
  // Probe on RegFile_r2o
  // Probe on RegFile_r4o
  Registers_File RegFile (
    .RegWrite(C4___C5_2_regw), .clk(Master_out), .BusW(C4___C5_r_q), .RB(ID_rt), .RA(ID_rs),
    .RW(C4___C5_rd_q), .BusA(RegFile_busa), .BusB(RegFile_busb), .R2O(RegFile_r2o), .R3O(RegFile_r3o),
    .R4O(RegFile_r4o), .R5O(RegFile_r5o), .R6O(RegFile_r6o), .R7O(RegFile_r7o), .R0O(RegFile_r0o),
    .R1O(RegFile_r1o));
  not not_1 (not_1_out, forward_stall_1_stall);
  Ctrls_Encoder Controls_Encoder (
    .Pass_By(ALU_Ctrl_pass_by), .STLU(ALU_Ctrl_slt_unsigned), .ALUOP(ALU_Ctrl_aluop),
    .ALUSRC(Main_Ctrl_alusrc), .RegW(Main_Ctrl_regw), .WBData(Main_Ctrl_wbdata), .MEMR(Main_Ctrl_memr),
    .MEMW(Main_Ctrl_memw), .Encoded_Controls(Controls_Encoder_encoded_controls), .BEQ(Main_Ctrl_beq),
    .BNE(Main_Ctrl_bne), .BLT(Main_Ctrl_blt), .BGE(Main_Ctrl_bge));
  // Probe on RegFile_r5o
  // Probe on RegFile_r6o
  Forward___Stall forward_stall_1 (
    .MEMRC3(C2___C3_2_memr), .Rs(ID_rs), .RdC3(C2___C3_rd_q), .RegWC3(C2___C3_2_regw), .RdC5(C4___C5_rd_q),
    .RegWC5(C4___C5_2_regw), .RdC4(C3___C4_rd_q), .RegWC4(C3___C4_2_regw), .Rt(ID_rt),
    .ForwardA(forward_stall_1_forwarda), .Stall(forward_stall_1_stall), .ForwardB(forward_stall_1_forwardb));
  Bubble_Ctrls Bubble_2 (
    .Stall(forward_stall_1_stall), .K2Cs(PC_Ctrl_k2cs), .ENC_Ctrls(Controls_Encoder_encoded_controls),
    .Controls(Bubble_2_controls));
  // Probe on RegFile_r7o
  Multiplexer #(.select(2), .width(16), .disabled(0), .enable("false")) multiplexer_3 (
    .in0(RegFile_busa), .in1(ALU_r), .in2(multiplexer_6_out), .in3(C4___C5_r_q), .out(multiplexer_3_out),
    .sel(forward_stall_1_forwarda));
  Multiplexer #(.select(2), .width(16), .disabled(0), .enable("false")) multiplexer_4 (
    .in0(RegFile_busb), .in1(ALU_r), .in2(multiplexer_6_out), .in3(C4___C5_r_q), .out(multiplexer_4_out),
    .sel(forward_stall_1_forwardb));
  ID_Pipe C2___C3 (
    .Clk(Master_out), .BTA_D(adder_2_out), .PC_1_D(C1___C2_pc_1_q), .LUI_D(LUI__11_shifted_16),
    ._5Imm_D(_5_bit_Ext_imm16), .A_D(multiplexer_3_out), .B_D(multiplexer_4_out), .Rd_D(multiplexer_1_out),
    .BTA_Q(C2___C3_bta_q), .PC_1_Q(C2___C3_pc_1_q), .LUI_Q(C2___C3_lui_q), ._5Imm_Q(C2___C3__5imm_q),
    .A_Q(C2___C3_a_q), .B_Q(C2___C3_b_q), .Rd_Q(C2___C3_rd_q));
  ALU_Ctrl_Pipe C2___C3_2 (
    .clk(Master_out), .Encoded_Controls_D(Bubble_2_controls), .Pass_By(C2___C3_2_pass_by),
    .SLTU(C2___C3_2_sltu), .ALUOP(C2___C3_2_aluop), .ALUSRC(C2___C3_2_alusrc),
    .Encoded_Controls_Q(C2___C3_2_encoded_controls_q), .RegW(C2___C3_2_regw), .BEQ(C2___C3_2_beq),
    .BNE(C2___C3_2_bne), .BLT(C2___C3_2_blt), .BGE(C2___C3_2_bge), .MEMR(C2___C3_2_memr));
  Multiplexer #(.width(16), .disabled(0), .enable("false")) multiplexer_5 (
    .in0(C2___C3_b_q), .in1(C2___C3__5imm_q), .out(multiplexer_5_out), .sel(C2___C3_2_alusrc));
  Arithmatic___Logic_Unit ALU (
    .A(C2___C3_a_q), .OP(C2___C3_2_aluop), .B(multiplexer_5_out), .SLTU(C2___C3_2_sltu), .R(ALU_r),
    .ZERO(ALU_zero), .LessThan(ALU_lessthan), .PC___1(C2___C3_pc_1_q), .LUI(C2___C3_lui_q),
    .Pass_By(C2___C3_2_pass_by));
  PC_Ctrl PC_Ctrl (
    .Zero(ALU_zero), .BEQ(C2___C3_2_beq), .BNE(C2___C3_2_bne), .BLT(C2___C3_2_blt), .BGE(C2___C3_2_bge),
    .Less_Than(ALU_lessthan), .Jump(Jump), .PCSrc(PCSrc), .K1Cs(PC_Ctrl_k1cs), .K2Cs(PC_Ctrl_k2cs));
  ALU_Pipe C3___C4 (
    .Clk(Master_out), .R_D(ALU_r), .B_D(C2___C3_b_q), .Rd_D(C2___C3_rd_q), .R_Q(C3___C4_r_q),
    .B_Q(C3___C4_b_q), .Rd_Q(C3___C4_rd_q));
  MEM_Ctrl_Pipe C3___C4_2 (
    .clk(Master_out), .Encoded_Controls_D(C2___C3_2_encoded_controls_q), .RegW(C3___C4_2_regw),
    .WBData(C3___C4_2_wbdata), .MEMR(C3___C4_2_memr), .MEMW(C3___C4_2_memw));
  Data_Memory DM (
    .Add(C3___C4_r_q), .Din(C3___C4_b_q), .MEMW(C3___C4_2_memw), .CLK(Master_out), .MEMR(C3___C4_2_memr),
    .Dout(DM_dout));
  Multiplexer #(.width(16), .disabled(0), .enable("false")) multiplexer_6 (
    .in0(C3___C4_r_q), .in1(DM_dout), .out(multiplexer_6_out), .sel(C3___C4_2_wbdata));
  MEM_Pipe C4___C5 (
    .Clk(Master_out), .R_D(multiplexer_6_out), .Rd_D(C3___C4_rd_q), .R_Q(C4___C5_r_q), .Rd_Q(C4___C5_rd_q));
  Rit_Ctrl_Pipe C4___C5_2 (.clk(Master_out), .Encoded_Controls_D(C3___C4_2_regw), .RegW(C4___C5_2_regw));
endmodule

module Registers_File (
  input  RegWrite,
  input  clk,
  input  [15:0] BusW,
  input  [2:0] RB,
  input  [2:0] RA,
  input  [2:0] RW,
  output [15:0] R0O,
  output [15:0] R1O,
  output [15:0] BusA,
  output [15:0] R2O,
  output [15:0] R3O,
  output [15:0] R4O,
  output [15:0] R5O,
  output [15:0] BusB,
  output [15:0] R6O,
  output [15:0] R7O
);

  wire _1, _2, _3, _4, _5, _6, _7, decoder_1_out1, decoder_1_out2, decoder_1_out3, decoder_1_out4,
       decoder_1_out5, decoder_1_out6, decoder_1_out7;

  Decoder #(.select(3), .enable("false")) decoder_1 (
    .out1(decoder_1_out1), .out2(decoder_1_out2), .out3(decoder_1_out3), .out4(decoder_1_out4),
    .out5(decoder_1_out5), .out6(decoder_1_out6), .out7(decoder_1_out7), .sel(RW));  // open: out0
  and and_1 (_1, RegWrite, decoder_1_out1);
  and and_2 (_2, RegWrite, decoder_1_out2);
  and and_3 (_3, RegWrite, decoder_1_out3);
  and and_4 (_4, RegWrite, decoder_1_out4);
  and and_5 (_5, RegWrite, decoder_1_out5);
  and and_6 (_6, RegWrite, decoder_1_out6);
  and and_7 (_7, RegWrite, decoder_1_out7);
  Register #(.width(16)) R1 (.D(BusW), .en(_1), .Q(R1O), .clk(clk));  // open: clr
  Register #(.width(16)) R2 (.D(BusW), .en(_2), .Q(R2O), .clk(clk));  // open: clr
  Register #(.width(16)) R3 (.D(BusW), .en(_3), .Q(R3O), .clk(clk));  // open: clr
  Register #(.width(16)) R4 (.D(BusW), .en(_4), .Q(R4O), .clk(clk));  // open: clr
  Register #(.width(16)) R5 (.D(BusW), .en(_5), .Q(R5O), .clk(clk));  // open: clr
  Register #(.width(16)) R6 (.D(BusW), .en(_6), .Q(R6O), .clk(clk));  // open: clr
  Register #(.width(16)) R7 (.D(BusW), .en(_7), .Q(R7O), .clk(clk));  // open: clr
  Multiplexer #(.select(3), .width(16), .disabled(0), .enable("false")) multiplexer_1 (
    .in0({16{1'b0}}), .in1(R1O), .in2(R2O), .in3(R3O), .in4(R4O), .in5(R5O), .in6(R6O), .in7(R7O),
    .out(BusA), .sel(RA));
  Multiplexer #(.select(3), .width(16), .disabled(0), .enable("false")) multiplexer_2 (
    .in0({16{1'b0}}), .in1(R1O), .in2(R2O), .in3(R3O), .in4(R4O), .in5(R5O), .in6(R6O), .in7(R7O),
    .out(BusB), .sel(RB));

  assign R0O = {16{1'b0}};
endmodule

module Instsruction_Decoder (
  input  [15:0] Instruction,
  output [4:0] OPCode,
  output [1:0] FUN,
  output [4:0] imm5,
  output [10:0] imm11,
  output [2:0] Rd,
  output [2:0] Rt,
  output [2:0] Rs
);


  assign FUN = Instruction[15:14];
  assign imm5 = Instruction[15:11];
  assign imm11 = Instruction[15:5];
  assign OPCode = Instruction[4:0];
  assign Rd = Instruction[13:11];
  assign Rs = Instruction[7:5];
  assign Rt = Instruction[10:8];
endmodule

module Data_Memory (
  input  [15:0] Add,
  input  [15:0] Din,
  input  MEMW,
  input  CLK,
  input  MEMR,
  output [15:0] Dout
);

  RAM #(.addrWidth(16), .dataWidth(16), .bus("separate")) ram_1 (
    .addr(Add), .din(Din), .data(Dout), .str(MEMW), .clk(CLK), .ld(MEMR));  // open: sel, clr
endmodule

module Instsruction_Memory (
  input  [15:0] ADD,
  input  clk,
  input  Enable,
  output [15:0] Inst
);

  RAM #(.addrWidth(16), .dataWidth(16)) ram_1 (.addr(ADD), .data(Inst), .clk(clk), .ld(Enable));  // open: sel, clr
endmodule

module ALU_Ctrl (
  input  [1:0] FUN,
  input  [4:0] OP,
  output SLT_Unsigned,
  output [3:0] ALUOP,
  output [1:0] Pass_By
);

  wire decoder_1_out0, decoder_1_out1, decoder_1_out2, decoder_1_out3, decoder_2_out0, decoder_2_out1,
       decoder_2_out2, decoder_2_out3, decoder_3_out0, decoder_3_out1, decoder_3_out2, decoder_3_out3,
       demultiplexer_1_out0, demultiplexer_1_out1, demultiplexer_1_out2, demultiplexer_1_out4,
       demultiplexer_1_out5, demultiplexer_1_out6, demultiplexer_1_out7, demultiplexer_1_out8,
       demultiplexer_1_out9, demultiplexer_1_out10, demultiplexer_1_out11, demultiplexer_1_out12,
       demultiplexer_1_out13, demultiplexer_1_out14, demultiplexer_1_out15, demultiplexer_1_out16,
       demultiplexer_1_out17, demultiplexer_1_out18, demultiplexer_1_out19, demultiplexer_1_out20,
       demultiplexer_1_out21, demultiplexer_1_out22, demultiplexer_1_out23, demultiplexer_1_out24,
       demultiplexer_1_out25, nor_1_out, or_1_out, or_2_out, or_3_out, or_4_out, or_5_out, or_6_out,
       or_7_out, or_8_out, or_10_out, or_11_out, or_12_out, or_13_out, or_14_out;

  Demultiplexer #(.select(5), .disabled(0), .enable("false")) demultiplexer_1 (
    .out0(demultiplexer_1_out0), .out1(demultiplexer_1_out1), .out2(demultiplexer_1_out2),
    .out4(demultiplexer_1_out4), .out5(demultiplexer_1_out5), .out6(demultiplexer_1_out6),
    .out7(demultiplexer_1_out7), .out8(demultiplexer_1_out8), .out9(demultiplexer_1_out9),
    .out10(demultiplexer_1_out10), .out11(demultiplexer_1_out11), .out12(demultiplexer_1_out12),
    .out13(demultiplexer_1_out13), .out14(demultiplexer_1_out14), .out15(demultiplexer_1_out15),
    .out16(demultiplexer_1_out16), .out17(demultiplexer_1_out17), .out18(demultiplexer_1_out18),
    .out19(demultiplexer_1_out19), .out20(demultiplexer_1_out20), .out21(demultiplexer_1_out21),
    .out22(demultiplexer_1_out22), .out23(demultiplexer_1_out23), .out24(demultiplexer_1_out24),
    .out25(demultiplexer_1_out25), .in(1'b1), .sel(OP));  // open: out3, out26, out27, out28, out29, out30, out31
  Decoder #(.select(2), .disabled(0)) decoder_1 (
    .out0(decoder_1_out0), .out1(decoder_1_out1), .out2(decoder_1_out2), .out3(decoder_1_out3), .sel(FUN),
    .en(demultiplexer_1_out0));
  Decoder #(.select(2), .disabled(0)) decoder_2 (
    .out0(decoder_2_out0), .out1(decoder_2_out1), .out2(decoder_2_out2), .out3(decoder_2_out3), .sel(FUN),
    .en(demultiplexer_1_out1));
  or or_1 (or_1_out, demultiplexer_1_out23, demultiplexer_1_out24, demultiplexer_1_out25, demultiplexer_1_out5);
  Decoder #(.select(2), .disabled(0)) decoder_3 (
    .out0(decoder_3_out0), .out1(decoder_3_out1), .out2(decoder_3_out2), .out3(decoder_3_out3), .sel(FUN),
    .en(demultiplexer_1_out2));
  or or_2 (or_2_out, decoder_3_out2, demultiplexer_1_out14);
  or or_3 (or_3_out, decoder_3_out3, demultiplexer_1_out15);
  or or_4 (or_4_out, decoder_1_out2, decoder_1_out3, demultiplexer_1_out6, demultiplexer_1_out7, demultiplexer_1_out20, demultiplexer_1_out21);
  or or_5 (or_5_out, decoder_2_out2, demultiplexer_1_out10);
  or or_6 (or_6_out, decoder_2_out3, demultiplexer_1_out11);
  or or_7 (or_7_out, decoder_3_out0, demultiplexer_1_out12);
  or or_8 (or_8_out, decoder_3_out1, demultiplexer_1_out13);
  or or_9 (SLT_Unsigned, decoder_1_out3, demultiplexer_1_out7);
  or or_10 (or_10_out, decoder_2_out0, demultiplexer_1_out8);
  or or_11 (or_11_out, decoder_2_out1, demultiplexer_1_out9);
  or or_12 (or_12_out, demultiplexer_1_out22, demultiplexer_1_out25);
  or or_13 (or_13_out, decoder_1_out0, demultiplexer_1_out4, demultiplexer_1_out22, demultiplexer_1_out16, demultiplexer_1_out17);
  or or_14 (or_14_out, decoder_1_out1, demultiplexer_1_out18, demultiplexer_1_out19);
  nor nor_1 (nor_1_out, or_12_out, demultiplexer_1_out23, demultiplexer_1_out5);
  Priority_Encoder #(.select(4), .disabled(0)) priority_encoder_1 (
    .in0(or_13_out), .in1(or_14_out), .in4(or_10_out), .in5(or_11_out), .in6(or_5_out), .in7(or_6_out),
    .in8(or_7_out), .in9(or_8_out), .in10(or_2_out), .in11(or_3_out), .in13(or_4_out), .in15(or_1_out),
    .out(ALUOP));  // open: in2, in3, in12, in14, gs, en_out, en_in
  Priority_Encoder #(.select(2)) priority_encoder_2 (
    .in0(nor_1_out), .in1(or_12_out), .in2(demultiplexer_1_out23), .in3(demultiplexer_1_out5), .out(Pass_By));  // open: gs, en_out, en_in

  // Other names for the same wires on the sheet: F[1:0] = FUN
endmodule

module Main_Ctrl (
  input  [4:0] OP,
  output [1:0] RegDst,
  output Ext,
  output WBData,
  output MEMR,
  output MEMW,
  output ALUSRC,
  output BEQ,
  output BNE,
  output BLT,
  output BGE,
  output RegW,
  output Imm11,
  output Jump,
  output LinkReg
);

  wire demultiplexer_1_out0, demultiplexer_1_out1, demultiplexer_1_out2, demultiplexer_1_out8,
       demultiplexer_1_out9, demultiplexer_1_out10, demultiplexer_1_out11, demultiplexer_1_out23,
       demultiplexer_1_out24, demultiplexer_1_out25, nor_1_out, or_1_out;

  Demultiplexer #(.select(5), .disabled(0), .enable("false")) demultiplexer_1 (
    .out0(demultiplexer_1_out0), .out1(demultiplexer_1_out1), .out2(demultiplexer_1_out2),
    .out8(demultiplexer_1_out8), .out9(demultiplexer_1_out9), .out10(demultiplexer_1_out10),
    .out11(demultiplexer_1_out11), .out16(MEMR), .out17(MEMW), .out18(BEQ), .out19(BNE), .out20(BLT),
    .out21(BGE), .out22(LinkReg), .out23(demultiplexer_1_out23), .out24(demultiplexer_1_out24),
    .out25(demultiplexer_1_out25), .in(1'b1), .sel(OP));  // open: out3, out4, out5, out6, out7, out12, out13, out14, out15, out26, out27, out28, out29, out30, out31
  or or_1 (or_1_out, demultiplexer_1_out0, demultiplexer_1_out1, demultiplexer_1_out2);
  nor nor_1 (nor_1_out, or_1_out, demultiplexer_1_out23, demultiplexer_1_out25);
  Priority_Encoder #(.select(2), .disabled(0)) priority_encoder_1 (
    .in0(nor_1_out), .in1(or_1_out), .in2(demultiplexer_1_out23), .in3(demultiplexer_1_out25), .out(RegDst));  // open: gs, en_out, en_in
  nor nor_2 (Ext, demultiplexer_1_out8, demultiplexer_1_out9, demultiplexer_1_out10, demultiplexer_1_out11);
  nor nor_3 (ALUSRC, or_1_out, BEQ, BNE, BLT, BGE);
  nor nor_4 (RegW, MEMW, BEQ, BNE, BLT, BGE, demultiplexer_1_out24);
  or or_2 (Imm11, demultiplexer_1_out24, demultiplexer_1_out25);
  or or_3 (Jump, Imm11, LinkReg);

  assign WBData = MEMR;
endmodule

module PC_Next (
  input  [4:0] imm5,
  input  [10:0] imm11,
  input  Imm_Type,
  input  [15:0] PC,
  input  [15:0] Ra,
  input  LinkReg,
  output [15:0] Imm5_11,
  output [15:0] PC_Ra
);

  wire [15:0] _5_bit_Ext_imm16, _11_bit_Ext_imm16;

  _5_bit_Extender _5_bit_Ext (.Sign(1'b1), .imm6(imm5), .imm16(_5_bit_Ext_imm16));
  _11_bit_Extender _11_bit_Ext (.Sign(1'b1), .imm11(imm11), .imm16(_11_bit_Ext_imm16));
  Multiplexer #(.width(16), .enable("false")) multiplexer_1 (
    .in0(_5_bit_Ext_imm16), .in1(_11_bit_Ext_imm16), .out(Imm5_11), .sel(Imm_Type));
  Multiplexer #(.width(16), .disabled(0), .enable("false")) multiplexer_2 (
    .in0(PC), .in1(Ra), .out(PC_Ra), .sel(LinkReg));
endmodule

module _5_bit_Extender (
  input  Sign,
  input  [4:0] imm6,
  output [15:0] imm16
);

  wire and_1_out;

  and and_1 (and_1_out, Sign, imm6[4]);
  assign imm16[15:5] = {{10{and_1_out}}, and_1_out};  // Bit_Extender bit_extender_1

  assign imm16[4:0] = imm6;
endmodule

module _11_bit_Extender (
  input  Sign,
  input  [10:0] imm11,
  output [15:0] imm16
);

  wire and_1_out;

  and and_1 (and_1_out, Sign, imm11[10]);
  assign imm16[15:11] = {{4{and_1_out}}, and_1_out};  // Bit_Extender bit_extender_1

  assign imm16[10:0] = imm11;
endmodule

module Arithmatic___Logic_Unit (
  input  [15:0] A,
  input  [3:0] OP,
  input  [15:0] B,
  input  SLTU,
  input  [1:0] Pass_By,
  input  [15:0] PC___1,
  input  [15:0] LUI,
  output [15:0] R,
  output ZERO,
  output LessThan
);

  wire OverFlow, R_Sign;
  wire [14:0] AU_o;
  wire [15:0] LU_o, multiplexer_1_out, SU_o;
  wire [15:1] SLT_slt;

  Arithmatic_Unit AU (.A(A), .SUB(OP[0]), .B(B), .O({R_Sign, AU_o}), .Overflow(OverFlow));
  Logic_Unit LU (.A(A), .B(B), .Sel(OP[1:0]), .O(LU_o));
  Shift_Unit SU (.A(A), .SA(B[3:0]), .Sel(OP[1:0]), .O(SU_o));
  Set_Less_Than_Unit SLT (
    .OF(OverFlow), .R_sign(R_Sign), .Sign_A(A[15]), .Sign_B(B[15]), .SLT({SLT_slt, LessThan}), .SLTU(SLTU));
  Multiplexer #(.select(2), .width(16), .disabled(0), .enable("false")) multiplexer_1 (
    .in0({R_Sign, AU_o}), .in1(LU_o), .in2(SU_o), .in3({SLT_slt, LessThan}), .out(multiplexer_1_out),
    .sel(OP[3:2]));
  Multiplexer #(.select(2), .width(16), .disabled(0), .enable("false")) multiplexer_2 (
    .in0(multiplexer_1_out), .in1(PC___1), .in2(LUI), .out(R), .sel(Pass_By));  // open: in3
  Comparator #(.width(16)) comparator_1 (.a(multiplexer_1_out), .b({16{1'b0}}), .eq(ZERO));  // open: gt, lt

  // Other names for the same wires on the sheet: sign_a = A[15]; SA[3:0] = B[3:0]; sign_b = B[15]; FUN[1:0] = OP[1:0];
  //   IOP[1:0] = OP[3:2]; Pass[1:0] = Pass_By
endmodule

module Logic_Unit (
  input  [15:0] A,
  input  [15:0] B,
  input  [1:0] Sel,
  output [15:0] O
);

  wire [15:0] and_1_out, not_1_out, or_1_out, xor_1_out;

  assign xor_1_out = A ^ B;  // XOR_Gate xor_1, 16 bits wide
  assign or_1_out = A | B;  // OR_Gate or_1, 16 bits wide
  assign and_1_out = A & B;  // AND_Gate and_1, 16 bits wide
  assign not_1_out = ~or_1_out;  // NOT_Gate not_1, 16 bits wide
  Multiplexer #(.select(2), .width(16), .disabled(0), .enable("false")) multiplexer_1 (
    .in0(xor_1_out), .in1(or_1_out), .in2(and_1_out), .in3(not_1_out), .out(O), .sel(Sel));
endmodule

module Arithmatic_Unit (
  input  [15:0] A,
  input  SUB,
  input  [15:0] B,
  output [15:0] O,
  output Overflow
);

  wire and_1_out, and_2_out, not_1_out, not_2_out, not_3_out;
  wire [15:0] multiplexer_1_out, xor_1_out;

  assign xor_1_out = B ^ {16{1'b1}};  // XOR_Gate xor_1, 16 bits wide
  Multiplexer #(.width(16), .disabled(0), .enable("false")) multiplexer_1 (
    .in0(B), .in1(xor_1_out), .out(multiplexer_1_out), .sel(SUB));
  not not_1 (not_1_out, A[15]);
  not not_2 (not_2_out, O[15]);
  not not_3 (not_3_out, multiplexer_1_out[15]);
  Adder #(.width(16)) adder_1 (.a(A), .b(multiplexer_1_out), .out(O), .cin(SUB));  // open: cout
  and and_1 (and_1_out, not_2_out, A[15], multiplexer_1_out[15]);
  and and_2 (and_2_out, O[15], not_1_out, not_3_out);
  or or_1 (Overflow, and_1_out, and_2_out);
endmodule

module Shift_Unit (
  input  [15:0] A,
  input  [3:0] SA,
  input  [1:0] Sel,
  output [15:0] O
);

  wire [15:0] shifter_1_out, shifter_2_out, shifter_3_out, shifter_4_out;

  Shifter #(.width(16)) shifter_1 (.in(A), .\dist (SA), .out(shifter_1_out));
  Shifter #(.width(16), .shift("lr")) shifter_2 (.in(A), .\dist (SA), .out(shifter_2_out));
  Shifter #(.width(16), .shift("ar")) shifter_3 (.in(A), .\dist (SA), .out(shifter_3_out));
  Shifter #(.width(16), .shift("rr")) shifter_4 (.in(A), .\dist (SA), .out(shifter_4_out));
  Multiplexer #(.select(2), .width(16), .disabled(0), .enable("false")) multiplexer_1 (
    .in0(shifter_1_out), .in1(shifter_2_out), .in2(shifter_3_out), .in3(shifter_4_out), .out(O), .sel(Sel));
endmodule

module Set_Less_Than_Unit (
  input  OF,
  input  R_sign,
  input  Sign_A,
  input  Sign_B,
  input  SLTU,
  output [15:0] SLT
);

  wire and_1_out, multiplexer_1_out, not_1_out, xor_1_out, xor_2_out;

  xor xor_1 (xor_1_out, OF, R_sign);
  xor xor_2 (xor_2_out, Sign_A, Sign_B);
  and and_1 (and_1_out, xor_1_out, xor_2_out);
  not not_1 (not_1_out, and_1_out);
  Multiplexer #(.disabled(0), .enable("false")) multiplexer_1 (
    .in0(xor_1_out), .in1(not_1_out), .out(multiplexer_1_out), .sel(SLTU));
  assign SLT = {{15{1'b0}}, multiplexer_1_out};  // Bit_Extender bit_extender_1
endmodule

module Load_Upper_Imm (
  input  [10:0] _11_bit_Imm,
  output [15:0] _11_shifted_16
);


  assign _11_shifted_16 = {_11_bit_Imm, {5{1'b0}}};
endmodule

module IF_Pipe (
  input  Clk,
  input  [15:0] PC_D,
  input  [15:0] PC_1_D,
  input  [15:0] Inst_D,
  output [15:0] PC_Q,
  output [15:0] PC_1_Q,
  output [15:0] Inst_Q
);

  Register #(.width(16)) register_1 (.D(PC_D), .en(1'b1), .Q(PC_Q), .clk(Clk), .clr(1'b0));
  Register #(.width(16)) register_2 (.D(PC_1_D), .en(1'b1), .Q(PC_1_Q), .clk(Clk), .clr(1'b0));
  Register #(.width(16)) register_3 (.D(Inst_D), .en(1'b1), .Q(Inst_Q), .clk(Clk), .clr(1'b0));
endmodule

module ID_Pipe (
  input  Clk,
  input  [15:0] BTA_D,
  input  [15:0] PC_1_D,
  input  [15:0] LUI_D,
  input  [15:0] _5Imm_D,
  input  [15:0] A_D,
  input  [15:0] B_D,
  input  [2:0] Rd_D,
  output [15:0] BTA_Q,
  output [15:0] PC_1_Q,
  output [15:0] LUI_Q,
  output [15:0] _5Imm_Q,
  output [15:0] A_Q,
  output [15:0] B_Q,
  output [2:0] Rd_Q
);

  Register #(.width(16)) register_1 (.D(BTA_D), .en(1'b1), .Q(BTA_Q), .clk(Clk), .clr(1'b0));
  Register #(.width(16)) register_2 (.D(PC_1_D), .en(1'b1), .Q(PC_1_Q), .clk(Clk), .clr(1'b0));
  Register #(.width(16)) register_3 (.D(LUI_D), .en(1'b1), .Q(LUI_Q), .clk(Clk), .clr(1'b0));
  Register #(.width(16)) register_4 (.D(_5Imm_D), .en(1'b1), .Q(_5Imm_Q), .clk(Clk), .clr(1'b0));
  Register #(.width(16)) register_5 (.D(A_D), .en(1'b1), .Q(A_Q), .clk(Clk), .clr(1'b0));
  Register #(.width(16)) register_6 (.D(B_D), .en(1'b1), .Q(B_Q), .clk(Clk), .clr(1'b0));
  Register #(.width(3)) register_7 (.D(Rd_D), .en(1'b1), .Q(Rd_Q), .clk(Clk), .clr(1'b0));
endmodule

module ALU_Pipe (
  input  Clk,
  input  [15:0] R_D,
  input  [15:0] B_D,
  input  [2:0] Rd_D,
  output [15:0] R_Q,
  output [15:0] B_Q,
  output [2:0] Rd_Q
);

  Register #(.width(16)) register_1 (.D(R_D), .en(1'b1), .Q(R_Q), .clk(Clk), .clr(1'b0));
  Register #(.width(16)) register_2 (.D(B_D), .en(1'b1), .Q(B_Q), .clk(Clk), .clr(1'b0));
  Register #(.width(3)) register_3 (.D(Rd_D), .en(1'b1), .Q(Rd_Q), .clk(Clk), .clr(1'b0));
endmodule

module MEM_Pipe (
  input  Clk,
  input  [15:0] R_D,
  input  [2:0] Rd_D,
  output [15:0] R_Q,
  output [2:0] Rd_Q
);

  Register #(.width(16)) register_1 (.D(R_D), .en(1'b1), .Q(R_Q), .clk(Clk), .clr(1'b0));
  Register #(.width(3)) register_2 (.D(Rd_D), .en(1'b1), .Q(Rd_Q), .clk(Clk), .clr(1'b0));
endmodule

module ALU_Ctrl_Pipe (
  input  clk,
  input  [15:0] Encoded_Controls_D,
  output [1:0] Pass_By,
  output SLTU,
  output [3:0] ALUOP,
  output ALUSRC,
  output BEQ,
  output BNE,
  output BLT,
  output BGE,
  output RegW,
  output MEMR,
  output [3:0] Encoded_Controls_Q
);

  Register #(.width(16)) register_1 (
    .D(Encoded_Controls_D), .en(1'b1),
    .Q({BGE, BLT, BNE, BEQ, Encoded_Controls_Q, ALUSRC, ALUOP, SLTU, Pass_By}), .clk(clk), .clr(1'b0));

  assign MEMR = Encoded_Controls_Q[2];
  assign RegW = Encoded_Controls_Q[0];
endmodule

module MEM_Ctrl_Pipe (
  input  clk,
  input  [3:0] Encoded_Controls_D,
  output RegW,
  output WBData,
  output MEMR,
  output MEMW
);

  Register #(.width(4)) register_1 (
    .D(Encoded_Controls_D), .en(1'b1), .Q({MEMW, MEMR, WBData, RegW}), .clk(clk), .clr(1'b0));
endmodule

module Rit_Ctrl_Pipe (
  input  clk,
  input  Encoded_Controls_D,
  output RegW
);

  Register #(.width(1)) register_1 (.D(Encoded_Controls_D), .en(1'b1), .Q(RegW), .clk(clk), .clr(1'b0));
endmodule

module Ctrls_Encoder (
  input  [1:0] Pass_By,
  input  STLU,
  input  [3:0] ALUOP,
  input  ALUSRC,
  input  RegW,
  input  WBData,
  input  MEMR,
  input  MEMW,
  input  BEQ,
  input  BNE,
  input  BLT,
  input  BGE,
  output [15:0] Encoded_Controls
);


  assign Encoded_Controls = {BGE, BLT, BNE, BEQ, MEMW, MEMR, WBData, RegW, ALUSRC, ALUOP, STLU, Pass_By};
endmodule

module Forward___Stall (
  input  MEMRC3,
  input  [2:0] Rs,
  input  [2:0] RdC3,
  input  RegWC3,
  input  [2:0] RdC5,
  input  RegWC5,
  input  [2:0] RdC4,
  input  RegWC4,
  input  [2:0] Rt,
  output [1:0] ForwardA,
  output Stall,
  output [1:0] ForwardB
);

  wire and_1_out, and_2_out, and_3_out, and_4_out, and_5_out, and_6_out, comparator_1_eq, comparator_2_eq,
       comparator_3_eq, comparator_4_eq, comparator_5_eq, comparator_6_eq, demultiplexer_1_out1,
       demultiplexer_1_out2, demultiplexer_1_out3, demultiplexer_1_out4, demultiplexer_1_out5,
       demultiplexer_1_out6, demultiplexer_1_out7, demultiplexer_2_out1, demultiplexer_2_out2,
       demultiplexer_2_out3, demultiplexer_2_out4, demultiplexer_2_out5, demultiplexer_2_out6,
       demultiplexer_2_out7, nor_1_out, nor_2_out, or_1_out, priority_encoder_1_gs, priority_encoder_2_gs;

  Demultiplexer #(.select(3), .disabled(0), .enable("false")) demultiplexer_1 (
    .out1(demultiplexer_1_out1), .out2(demultiplexer_1_out2), .out3(demultiplexer_1_out3),
    .out4(demultiplexer_1_out4), .out5(demultiplexer_1_out5), .out6(demultiplexer_1_out6),
    .out7(demultiplexer_1_out7), .in(1'b1), .sel(Rs));  // open: out0
  Demultiplexer #(.select(3), .disabled(0), .enable("false")) demultiplexer_2 (
    .out1(demultiplexer_2_out1), .out2(demultiplexer_2_out2), .out3(demultiplexer_2_out3),
    .out4(demultiplexer_2_out4), .out5(demultiplexer_2_out5), .out6(demultiplexer_2_out6),
    .out7(demultiplexer_2_out7), .in(1'b1), .sel(Rt));  // open: out0
  Priority_Encoder priority_encoder_1 (
    .in1(demultiplexer_1_out1), .in2(demultiplexer_1_out2), .in3(demultiplexer_1_out3),
    .in4(demultiplexer_1_out4), .in5(demultiplexer_1_out5), .in6(demultiplexer_1_out6),
    .in7(demultiplexer_1_out7), .gs(priority_encoder_1_gs));  // open: in0, out, en_in, en_out
  Priority_Encoder priority_encoder_2 (
    .in1(demultiplexer_2_out1), .in2(demultiplexer_2_out2), .in3(demultiplexer_2_out3),
    .in4(demultiplexer_2_out4), .in5(demultiplexer_2_out5), .in6(demultiplexer_2_out6),
    .in7(demultiplexer_2_out7), .gs(priority_encoder_2_gs));  // open: in0, out, en_in, en_out
  and and_1 (and_1_out, priority_encoder_1_gs, comparator_1_eq, RegWC3);
  Comparator #(.width(3), .mode("unsigned")) comparator_1 (.a(Rs), .b(RdC3), .eq(comparator_1_eq));  // open: gt, lt
  and and_2 (and_2_out, priority_encoder_1_gs, comparator_2_eq, RegWC4);
  Comparator #(.width(3), .mode("unsigned")) comparator_2 (.a(Rs), .b(RdC4), .eq(comparator_2_eq));  // open: gt, lt
  Comparator #(.width(3), .mode("unsigned")) comparator_3 (.a(Rs), .b(RdC5), .eq(comparator_3_eq));  // open: gt, lt
  and and_3 (and_3_out, priority_encoder_1_gs, comparator_3_eq, RegWC5);
  Comparator #(.width(3), .mode("unsigned")) comparator_4 (.a(RdC5), .b(Rt), .eq(comparator_4_eq));  // open: gt, lt
  and and_4 (and_4_out, RegWC5, comparator_4_eq, priority_encoder_2_gs);
  Comparator #(.width(3), .mode("unsigned")) comparator_5 (.a(RdC4), .b(Rt), .eq(comparator_5_eq));  // open: gt, lt
  and and_5 (and_5_out, RegWC4, comparator_5_eq, priority_encoder_2_gs);
  and and_6 (and_6_out, RegWC3, comparator_6_eq, priority_encoder_2_gs);
  Comparator #(.width(3), .mode("unsigned")) comparator_6 (.a(RdC3), .b(Rt), .eq(comparator_6_eq));  // open: gt, lt
  nor nor_1 (nor_1_out, and_1_out, and_2_out, and_3_out);
  nor nor_2 (nor_2_out, and_4_out, and_5_out, and_6_out);
  Priority_Encoder #(.select(2)) priority_encoder_3 (
    .in0(nor_1_out), .in1(and_1_out), .in2(and_2_out), .in3(and_3_out), .out(ForwardA));  // open: gs, en_out, en_in
  or or_1 (or_1_out, and_1_out, and_6_out);
  Priority_Encoder #(.select(2)) priority_encoder_4 (
    .in0(nor_2_out), .in1(and_6_out), .in2(and_5_out), .in3(and_4_out), .out(ForwardB));  // open: gs, en_out, en_in
  and and_7 (Stall, MEMRC3, or_1_out);
endmodule

module PC_Ctrl (
  input  Jump,
  input  Zero,
  input  BEQ,
  input  BNE,
  input  BLT,
  input  BGE,
  input  Less_Than,
  output [1:0] PCSrc,
  output K1Cs,
  output K2Cs
);

  wire and_1_out, and_2_out, and_3_out, and_4_out, nor_1_out, not_1_out, not_2_out;

  not not_1 (not_1_out, Zero);
  not not_2 (not_2_out, Less_Than);
  and and_1 (and_1_out, Zero, BEQ);
  and and_2 (and_2_out, not_1_out, BNE);
  and and_3 (and_3_out, BLT, Less_Than);
  and and_4 (and_4_out, BGE, not_2_out);
  or or_1 (K2Cs, and_1_out, and_2_out, and_3_out, and_4_out);
  nor nor_1 (nor_1_out, Jump, K2Cs);
  or or_2 (K1Cs, Jump, K2Cs);
  Priority_Encoder #(.select(2)) priority_encoder_1 (
    .in0(nor_1_out), .in1(Jump), .in2(K2Cs), .out(PCSrc));  // open: in3, gs, en_out, en_in
endmodule

module Bubble_Ctrls (
  input  Stall,
  input  K2Cs,
  input  [15:0] ENC_Ctrls,
  output [15:0] Controls
);

  wire or_1_out;

  or or_1 (or_1_out, Stall, K2Cs);
  Multiplexer #(.width(16), .disabled(0), .enable("false")) multiplexer_1 (
    .in0(ENC_Ctrls), .in1(16'h3), .out(Controls), .sel(or_1_out));
endmodule

module Bubble_Inst (
  input  K1Cs,
  input  [15:0] Valid_nstruction,
  output [15:0] Instruction
);

  Multiplexer #(.width(16), .disabled(0), .enable("false")) multiplexer_1 (
    .in0(Valid_nstruction), .in1(16'h5), .out(Instruction), .sel(K1Cs));
endmodule
