// Logisim project SC Processor.circ as structural Verilog: 17 circuits, main circuit Data Path
module Data_Path (
  output [15:0] R3,
  output [15:0] R4,
  output [15:0] R2,
  output [15:0] R5,
  output [15:0] R1,
  output [15:0] R6,
  output [15:0] R0,
  output [15:0] R7
);

  wire ALU_Ctrl_slt_unsigned, ALUSrc, Ext, LR, LT, Master_out, MemR, MemW, RegW, Zero;
  wire [1:0] ID_fun, PC_Ctrl_pc_ctrl, RegDst, WBData;
  wire [2:0] ID_rd, ID_rs, ID_rt, multiplexer_1_out;
  wire [3:0] ALU_Ctrl_aluop;
  wire [4:0] ID_imm5, ID_opcode;
  wire [10:0] ID_imm11;
  wire [15:0] _5_bit_Ext_imm16, adder_1_out, adder_2_out, ALU_r, DM_dout, IM_inst, LUI__11_shifted_16,
       multiplexer_2_out, multiplexer_3_out, multiplexer_4_out, PC_Offset_offset, PC_q, RegFile_busa,
       RegFile_busb;

  Clock Master (.out(Master_out));
  PC_Ctrl PC_Ctrl (.Zero(Zero), .OP(ID_opcode), .Less_Than(LT), .PC_Ctrl(PC_Ctrl_pc_ctrl), .LinkReg(LR));
  Register #(.width(16)) PC (.D(adder_1_out), .Q(PC_q), .clk(Master_out));  // open: en, clr
  Instsruction_Decoder ID (
    .Instruction(IM_inst), .OPCode(ID_opcode), .FUN(ID_fun), .imm5(ID_imm5), .imm11(ID_imm11), .Rd(ID_rd),
    .Rt(ID_rt), .Rs(ID_rs));
  Instsruction_Memory IM (.Add(PC_q), .clkl(Master_out), .Inst(IM_inst));
  PC_Next PC_Offset (.one(16'h1), .imm5(ID_imm5), .imm11(ID_imm11), .Offset(PC_Offset_offset), .PCSrc(PC_Ctrl_pc_ctrl));
  Load_Upper_Imm LUI (._11_bit_Imm(ID_imm11), ._11_shifted_16(LUI__11_shifted_16));
  Multiplexer #(.select(2), .width(3), .disabled(0), .enable("false")) multiplexer_1 (
    .in0(ID_rt), .in1(ID_rd), .in2(3'b001), .in3(3'b111), .out(multiplexer_1_out), .sel(RegDst));
  Adder #(.width(16)) adder_1 (.a(PC_Offset_offset), .b(multiplexer_2_out), .out(adder_1_out));  // open: cin, cout
  Multiplexer #(.width(16), .disabled(0), .enable("false")) multiplexer_2 (
    .in0(PC_q), .in1(RegFile_busa), .out(multiplexer_2_out), .sel(LR));
  Adder #(.width(16)) adder_2 (.a(PC_q), .b(16'h1), .out(adder_2_out));  // open: cin, cout
  _5_bit_Extender _5_bit_Ext (.Sign(Ext), .imm5(ID_imm5), .imm16(_5_bit_Ext_imm16));
  Main_Ctrl Main_Ctrl (
    .OP(ID_opcode), .RegDst(RegDst), .WBData(WBData), .Ext(Ext), .MEMR(MemR), .MEMW(MemW), .ALUSRC(ALUSrc),
    .RegW(RegW));
  Registers_File RegFile (
    .RegWrite(RegW), .clk(Master_out), .BusW(multiplexer_4_out), .RB(ID_rt), .RA(ID_rs),
    .RW(multiplexer_1_out), .BusA(RegFile_busa), .BusB(RegFile_busb), .R2O(R2), .R3O(R3), .R4O(R4), .R5O(R5),
    .R6O(R6), .R7O(R7), .R0O(R0), .R1O(R1));
  Multiplexer #(.width(16), .disabled(0), .enable("false")) multiplexer_3 (
    .in0(RegFile_busb), .in1(_5_bit_Ext_imm16), .out(multiplexer_3_out), .sel(ALUSrc));
  ALU_Ctrl ALU_Ctrl (.FUN(ID_fun), .OP(ID_opcode), .ALUOP(ALU_Ctrl_aluop), .SLT_Unsigned(ALU_Ctrl_slt_unsigned));
  Arithmatic___Logic_Unit ALU (
    .A(RegFile_busa), .OP(ALU_Ctrl_aluop), .B(multiplexer_3_out), .SLTU(ALU_Ctrl_slt_unsigned), .R(ALU_r),
    .ZERO(Zero), .LessThan(LT));
  Data_Memory DM (.Add(ALU_r), .Din(RegFile_busb), .MEMW(MemW), .CLK(Master_out), .MEMR(MemR), .Dout(DM_dout));
  Multiplexer #(.select(2), .width(16), .disabled(0), .enable("false")) multiplexer_4 (
    .in0(ALU_r), .in1(DM_dout), .in2(LUI__11_shifted_16), .in3(adder_2_out), .out(multiplexer_4_out),
    .sel(WBData));
endmodule

module Registers_File (
  input  RegWrite,
  input  clk,
  input  [15:0] BusW,
  input  [2:0] RB,
  input  [2:0] RA,
  input  [2:0] RW,
  output [15:0] R0O,
  output [15:0] R1O,
  output [15:0] BusA,
  output [15:0] R2O,
  output [15:0] R3O,
  output [15:0] R4O,
  output [15:0] R5O,
  output [15:0] BusB,
  output [15:0] R6O,
  output [15:0] R7O
);

  wire _1, _2, _3, _4, _5, _6, _7, decoder_1_out1, decoder_1_out2, decoder_1_out3, decoder_1_out4,
       decoder_1_out5, decoder_1_out6, decoder_1_out7;

  Decoder #(.select(3), .enable("false")) decoder_1 (
    .out1(decoder_1_out1), .out2(decoder_1_out2), .out3(decoder_1_out3), .out4(decoder_1_out4),
    .out5(decoder_1_out5), .out6(decoder_1_out6), .out7(decoder_1_out7), .sel(RW));  // open: out0
  and and_1 (_1, RegWrite, decoder_1_out1);
  and and_2 (_2, RegWrite, decoder_1_out2);
  and and_3 (_3, RegWrite, decoder_1_out3);
  and and_4 (_4, RegWrite, decoder_1_out4);
  and and_5 (_5, RegWrite, decoder_1_out5);
  and and_6 (_6, RegWrite, decoder_1_out6);
  and and_7 (_7, RegWrite, decoder_1_out7);
  Register #(.width(16)) R1 (.D(BusW), .en(_1), .Q(R1O), .clk(clk));  // open: clr
  Register #(.width(16)) R2 (.D(BusW), .en(_2), .Q(R2O), .clk(clk));  // open: clr
  Register #(.width(16)) R3 (.D(BusW), .en(_3), .Q(R3O), .clk(clk));  // open: clr
  Register #(.width(16)) R4 (.D(BusW), .en(_4), .Q(R4O), .clk(clk));  // open: clr
  Register #(.width(16)) R5 (.D(BusW), .en(_5), .Q(R5O), .clk(clk));  // open: clr
  Register #(.width(16)) R6 (.D(BusW), .en(_6), .Q(R6O), .clk(clk));  // open: clr
  Register #(.width(16)) R7 (.D(BusW), .en(_7), .Q(R7O), .clk(clk));  // open: clr
  Multiplexer #(.select(3), .width(16), .disabled(0), .enable("false")) multiplexer_1 (
    .in0({16{1'b0}}), .in1(R1O), .in2(R2O), .in3(R3O), .in4(R4O), .in5(R5O), .in6(R6O), .in7(R7O),
    .out(BusA), .sel(RA));
  Multiplexer #(.select(3), .width(16), .disabled(0), .enable("false")) multiplexer_2 (
    .in0({16{1'b0}}), .in1(R1O), .in2(R2O), .in3(R3O), .in4(R4O), .in5(R5O), .in6(R6O), .in7(R7O),
    .out(BusB), .sel(RB));

  assign R0O = {16{1'b0}};
endmodule

module Instsruction_Decoder (
  input  [15:0] Instruction,
  output [4:0] OPCode,
  output [1:0] FUN,
  output [4:0] imm5,
  output [10:0] imm11,
  output [2:0] Rd,
  output [2:0] Rt,
  output [2:0] Rs
);


  assign FUN = Instruction[15:14];
  assign imm5 = Instruction[15:11];
  assign imm11 = Instruction[15:5];
  assign OPCode = Instruction[4:0];
  assign Rd = Instruction[13:11];
  assign Rs = Instruction[7:5];
  assign Rt = Instruction[10:8];
endmodule

module Data_Memory (
  input  [15:0] Add,
  input  [15:0] Din,
  input  MEMW,
  input  CLK,
  input  MEMR,
  output [15:0] Dout
);

  RAM #(.addrWidth(16), .dataWidth(16), .bus("separate")) ram_1 (
    .addr(Add), .din(Din), .data(Dout), .str(MEMW), .clk(CLK), .ld(MEMR));  // open: sel, clr
endmodule

module Instsruction_Memory (
  input  [15:0] Add,
  input  clkl,
  output [15:0] Inst
);

  RAM #(.addrWidth(16), .dataWidth(16)) ram_1 (.addr(Add), .data(Inst), .clk(clkl), .ld(1'b1));  // open: sel, clr
endmodule

module ALU_Ctrl (
  input  [1:0] FUN,
  input  [4:0] OP,
  output SLT_Unsigned,
  output [3:0] ALUOP
);

  wire decoder_1_out0, decoder_1_out1, decoder_1_out2, decoder_1_out3, decoder_2_out0, decoder_2_out1,
       decoder_2_out2, decoder_2_out3, decoder_3_out0, decoder_3_out1, decoder_3_out2, decoder_3_out3,
       demultiplexer_1_out0, demultiplexer_1_out1, demultiplexer_1_out2, demultiplexer_1_out4,
       demultiplexer_1_out6, demultiplexer_1_out7, demultiplexer_1_out8, demultiplexer_1_out9,
       demultiplexer_1_out10, demultiplexer_1_out11, demultiplexer_1_out12, demultiplexer_1_out13,
       demultiplexer_1_out14, demultiplexer_1_out15, demultiplexer_1_out16, demultiplexer_1_out17,
       demultiplexer_1_out18, demultiplexer_1_out19, demultiplexer_1_out20, demultiplexer_1_out21,
       demultiplexer_1_out22, demultiplexer_1_out23, demultiplexer_1_out24, demultiplexer_1_out25, or_1_out,
       or_2_out, or_3_out, or_4_out, or_5_out, or_6_out, or_7_out, or_8_out, or_10_out, or_11_out, or_12_out,
       or_13_out;

  Demultiplexer #(.select(5), .disabled(0), .enable("false")) demultiplexer_1 (
    .out0(demultiplexer_1_out0), .out1(demultiplexer_1_out1), .out2(demultiplexer_1_out2),
    .out4(demultiplexer_1_out4), .out6(demultiplexer_1_out6), .out7(demultiplexer_1_out7),
    .out8(demultiplexer_1_out8), .out9(demultiplexer_1_out9), .out10(demultiplexer_1_out10),
    .out11(demultiplexer_1_out11), .out12(demultiplexer_1_out12), .out13(demultiplexer_1_out13),
    .out14(demultiplexer_1_out14), .out15(demultiplexer_1_out15), .out16(demultiplexer_1_out16),
    .out17(demultiplexer_1_out17), .out18(demultiplexer_1_out18), .out19(demultiplexer_1_out19),
    .out20(demultiplexer_1_out20), .out21(demultiplexer_1_out21), .out22(demultiplexer_1_out22),
    .out23(demultiplexer_1_out23), .out24(demultiplexer_1_out24), .out25(demultiplexer_1_out25), .in(1'b1),
    .sel(OP));  // open: out3, out5, out26, out27, out28, out29, out30, out31
  Decoder #(.select(2), .disabled(0)) decoder_1 (
    .out0(decoder_1_out0), .out1(decoder_1_out1), .out2(decoder_1_out2), .out3(decoder_1_out3), .sel(FUN),
    .en(demultiplexer_1_out0));
  Decoder #(.select(2), .disabled(0)) decoder_2 (
    .out0(decoder_2_out0), .out1(decoder_2_out1), .out2(decoder_2_out2), .out3(decoder_2_out3), .sel(FUN),
    .en(demultiplexer_1_out1));
  or or_1 (or_1_out, demultiplexer_1_out23, demultiplexer_1_out24, demultiplexer_1_out25);
  Decoder #(.select(2), .disabled(0)) decoder_3 (
    .out0(decoder_3_out0), .out1(decoder_3_out1), .out2(decoder_3_out2), .out3(decoder_3_out3), .sel(FUN),
    .en(demultiplexer_1_out2));
  or or_2 (or_2_out, decoder_3_out2, demultiplexer_1_out14);
  or or_3 (or_3_out, decoder_3_out3, demultiplexer_1_out15);
  or or_4 (or_4_out, decoder_1_out2, decoder_1_out3, demultiplexer_1_out6, demultiplexer_1_out7, demultiplexer_1_out20, demultiplexer_1_out21);
  or or_5 (or_5_out, decoder_2_out2, demultiplexer_1_out10);
  or or_6 (or_6_out, decoder_2_out3, demultiplexer_1_out11);
  or or_7 (or_7_out, decoder_3_out0, demultiplexer_1_out12);
  or or_8 (or_8_out, decoder_3_out1, demultiplexer_1_out13);
  or or_9 (SLT_Unsigned, decoder_1_out3, demultiplexer_1_out7);
  or or_10 (or_10_out, decoder_2_out0, demultiplexer_1_out8);
  or or_11 (or_11_out, decoder_2_out1, demultiplexer_1_out9);
  or or_12 (or_12_out, decoder_1_out0, demultiplexer_1_out4, demultiplexer_1_out22, demultiplexer_1_out16, demultiplexer_1_out17);
  or or_13 (or_13_out, decoder_1_out1, demultiplexer_1_out18, demultiplexer_1_out19);
  Priority_Encoder #(.select(4), .disabled(0)) priority_encoder_1 (
    .in0(or_12_out), .in1(or_13_out), .in4(or_10_out), .in5(or_11_out), .in6(or_5_out), .in7(or_6_out),
    .in8(or_7_out), .in9(or_8_out), .in10(or_2_out), .in11(or_3_out), .in13(or_4_out), .in15(or_1_out),
    .out(ALUOP));  // open: in2, in3, in12, in14, gs, en_out, en_in

  // Other names for the same wires on the sheet: F[1:0] = FUN
endmodule

module Main_Ctrl (
  input  [4:0] OP,
  output [1:0] RegDst,
  output [1:0] WBData,
  output Ext,
  output MEMR,
  output MEMW,
  output ALUSRC,
  output RegW
);

  wire demultiplexer_1_out0, demultiplexer_1_out1, demultiplexer_1_out2, demultiplexer_1_out8,
       demultiplexer_1_out9, demultiplexer_1_out10, demultiplexer_1_out11, demultiplexer_1_out18,
       demultiplexer_1_out19, demultiplexer_1_out20, demultiplexer_1_out21, demultiplexer_1_out22,
       demultiplexer_1_out23, demultiplexer_1_out24, demultiplexer_1_out25, nor_1_out, nor_2_out, or_1_out,
       or_2_out;

  Demultiplexer #(.select(5), .disabled(0), .enable("false")) demultiplexer_1 (
    .out0(demultiplexer_1_out0), .out1(demultiplexer_1_out1), .out2(demultiplexer_1_out2),
    .out8(demultiplexer_1_out8), .out9(demultiplexer_1_out9), .out10(demultiplexer_1_out10),
    .out11(demultiplexer_1_out11), .out16(MEMR), .out17(MEMW), .out18(demultiplexer_1_out18),
    .out19(demultiplexer_1_out19), .out20(demultiplexer_1_out20), .out21(demultiplexer_1_out21),
    .out22(demultiplexer_1_out22), .out23(demultiplexer_1_out23), .out24(demultiplexer_1_out24),
    .out25(demultiplexer_1_out25), .in(1'b1), .sel(OP));  // open: out3, out4, out5, out6, out7, out12, out13, out14, out15, out26, out27, out28, out29, out30, out31
  or or_1 (or_1_out, demultiplexer_1_out0, demultiplexer_1_out1, demultiplexer_1_out2);
  nor nor_1 (nor_1_out, or_1_out, demultiplexer_1_out23, demultiplexer_1_out25);
  or or_2 (or_2_out, demultiplexer_1_out25, demultiplexer_1_out22);
  Priority_Encoder #(.select(2), .disabled(0)) priority_encoder_1 (
    .in0(nor_1_out), .in1(or_1_out), .in2(demultiplexer_1_out23), .in3(demultiplexer_1_out25), .out(RegDst));  // open: gs, en_out, en_in
  nor nor_2 (nor_2_out, or_2_out, demultiplexer_1_out23, MEMR);
  nor nor_3 (Ext, demultiplexer_1_out8, demultiplexer_1_out9, demultiplexer_1_out10, demultiplexer_1_out11);
  nor nor_4 (ALUSRC, or_1_out, demultiplexer_1_out18, demultiplexer_1_out19, demultiplexer_1_out20, demultiplexer_1_out21);
  nor nor_5 (RegW, MEMW, demultiplexer_1_out18, demultiplexer_1_out19, demultiplexer_1_out20, demultiplexer_1_out21, demultiplexer_1_out24);
  Priority_Encoder #(.select(2), .disabled(0)) priority_encoder_2 (
    .in0(nor_2_out), .in1(MEMR), .in2(demultiplexer_1_out23), .in3(or_2_out), .out(WBData));  // open: gs, en_out, en_in
endmodule

module PC_Ctrl (
  input  Zero,
  input  [4:0] OP,
  input  Less_Than,
  output [1:0] PC_Ctrl,
  output LinkReg
);

  wire and_1_out, and_2_out, and_3_out, and_4_out, demultiplexer_1_out0, demultiplexer_1_out1,
       demultiplexer_1_out2, demultiplexer_1_out18, demultiplexer_1_out19, demultiplexer_1_out20,
       demultiplexer_1_out21, demultiplexer_1_out24, demultiplexer_1_out25, nor_1_out, not_1_out, not_2_out,
       or_1_out, or_2_out, or_3_out, or_4_out;

  Demultiplexer #(.select(5), .disabled(0), .enable("false")) demultiplexer_1 (
    .out0(demultiplexer_1_out0), .out1(demultiplexer_1_out1), .out2(demultiplexer_1_out2),
    .out18(demultiplexer_1_out18), .out19(demultiplexer_1_out19), .out20(demultiplexer_1_out20),
    .out21(demultiplexer_1_out21), .out22(LinkReg), .out24(demultiplexer_1_out24),
    .out25(demultiplexer_1_out25), .in(1'b1), .sel(OP));  // open: out3, out4, out5, out6, out7, out8, out9, out10, out11, out12, out13, out14, out15, out16, out17, out23, out26, out27, out28, out29, out30, out31
  or or_1 (or_1_out, demultiplexer_1_out0, demultiplexer_1_out1, demultiplexer_1_out2);
  not not_1 (not_1_out, Zero);
  not not_2 (not_2_out, Less_Than);
  or or_2 (or_2_out, demultiplexer_1_out24, demultiplexer_1_out25);
  and and_1 (and_1_out, Zero, demultiplexer_1_out18);
  and and_2 (and_2_out, not_1_out, demultiplexer_1_out19);
  and and_3 (and_3_out, demultiplexer_1_out20, Less_Than);
  and and_4 (and_4_out, demultiplexer_1_out21, not_2_out);
  or or_3 (or_3_out, and_1_out, and_2_out, LinkReg, and_3_out, and_4_out);
  or or_4 (or_4_out, or_1_out, nor_1_out);
  nor nor_1 (nor_1_out, or_3_out, or_2_out);
  Priority_Encoder #(.select(2)) priority_encoder_1 (
    .in0(or_4_out), .in1(or_3_out), .in2(or_2_out), .out(PC_Ctrl));  // open: in3, gs, en_out, en_in

  // Other names for the same wires on the sheet: L = Less_Than; Z = Zero
endmodule

module PC_Next (
  input  [15:0] one,
  input  [4:0] imm5,
  input  [1:0] PCSrc,
  input  [10:0] imm11,
  output [15:0] Offset
);

  wire [15:0] _5_bit_Ext_imm16, _11_bit_Ext_imm16;

  _5_bit_Extender _5_bit_Ext (.Sign(1'b1), .imm5(imm5), .imm16(_5_bit_Ext_imm16));
  _11_bit_Extender _11_bit_Ext (.Sign(1'b1), .imm11(imm11), .imm16(_11_bit_Ext_imm16));
  Multiplexer #(.select(2), .width(16), .enable("false")) multiplexer_1 (
    .in0(one), .in1(_5_bit_Ext_imm16), .in2(_11_bit_Ext_imm16), .out(Offset), .sel(PCSrc));  // open: in3
endmodule

module _5_bit_Extender (
  input  Sign,
  input  [4:0] imm5,
  output [15:0] imm16
);

  wire and_1_out;

  and and_1 (and_1_out, Sign, imm5[4]);
  assign imm16[15:5] = {{10{and_1_out}}, and_1_out};  // Bit_Extender bit_extender_1

  assign imm16[4:0] = imm5;
endmodule

module _11_bit_Extender (
  input  Sign,
  input  [10:0] imm11,
  output [15:0] imm16
);

  wire and_1_out;

  and and_1 (and_1_out, Sign, imm11[10]);
  assign imm16[15:11] = {{4{and_1_out}}, and_1_out};  // Bit_Extender bit_extender_1

  assign imm16[10:0] = imm11;
endmodule

module Arithmatic___Logic_Unit (
  input  [15:0] A,
  input  [3:0] OP,
  input  [15:0] B,
  input  SLTU,
  output [15:0] R,
  output ZERO,
  output LessThan
);

  wire OverFlow, R_Sign;
  wire [14:0] AU_o;
  wire [15:0] LU_o, SU_o;
  wire [15:1] SLT_slt;

  Arithmatic_Unit AU (.A(A), .SUB(OP[0]), .B(B), .O({R_Sign, AU_o}), .Overflow(OverFlow));
  Logic_Unit LU (.A(A), .B(B), .Sel(OP[1:0]), .O(LU_o));
  Shift_Unit SU (.A(A), .SA(B[3:0]), .Sel(OP[1:0]), .O(SU_o));
  Set_Less_Than_Unit SLT (
    .OF(OverFlow), .R_sign(R_Sign), .Sign_A(A[15]), .Sign_B(B[15]), .SLT({SLT_slt, LessThan}), .SLTU(SLTU));
  Multiplexer #(.select(2), .width(16), .disabled(0), .enable("false")) multiplexer_1 (
    .in0({R_Sign, AU_o}), .in1(LU_o), .in2(SU_o), .in3({SLT_slt, LessThan}), .out(R), .sel(OP[3:2]));
  Comparator #(.width(16)) comparator_1 (.a(R), .b({16{1'b0}}), .eq(ZERO));  // open: gt, lt

  // Other names for the same wires on the sheet: sign_a = A[15]; SA[3:0] = B[3:0]; sign_b = B[15]; FUN[1:0] = OP[1:0];
  //   IOP[1:0] = OP[3:2]
endmodule

module Logic_Unit (
  input  [15:0] A,
  input  [15:0] B,
  input  [1:0] Sel,
  output [15:0] O
);

  wire [15:0] and_1_out, not_1_out, or_1_out, xor_1_out;

  assign xor_1_out = A ^ B;  // XOR_Gate xor_1, 16 bits wide
  assign or_1_out = A | B;  // OR_Gate or_1, 16 bits wide
  assign and_1_out = A & B;  // AND_Gate and_1, 16 bits wide
  assign not_1_out = ~or_1_out;  // NOT_Gate not_1, 16 bits wide
  Multiplexer #(.select(2), .width(16), .disabled(0), .enable("false")) multiplexer_1 (
    .in0(xor_1_out), .in1(or_1_out), .in2(and_1_out), .in3(not_1_out), .out(O), .sel(Sel));
endmodule

module Arithmatic_Unit (
  input  [15:0] A,
  input  SUB,
  input  [15:0] B,
  output [15:0] O,
  output Overflow
);

  wire and_1_out, and_2_out, not_1_out, not_2_out, not_3_out;
  wire [15:0] multiplexer_1_out, xor_1_out;

  assign xor_1_out = B ^ {16{1'b1}};  // XOR_Gate xor_1, 16 bits wide
  Multiplexer #(.width(16), .disabled(0), .enable("false")) multiplexer_1 (
    .in0(B), .in1(xor_1_out), .out(multiplexer_1_out), .sel(SUB));
  not not_1 (not_1_out, A[15]);
  not not_2 (not_2_out, O[15]);
  not not_3 (not_3_out, multiplexer_1_out[15]);
  Adder #(.width(16)) adder_1 (.a(A), .b(multiplexer_1_out), .out(O), .cin(SUB));  // open: cout
  and and_1 (and_1_out, not_2_out, A[15], multiplexer_1_out[15]);
  and and_2 (and_2_out, O[15], not_1_out, not_3_out);
  or or_1 (Overflow, and_1_out, and_2_out);
endmodule

module Shift_Unit (
  input  [15:0] A,
  input  [3:0] SA,
  input  [1:0] Sel,
  output [15:0] O
);

  wire [15:0] shifter_1_out, shifter_2_out, shifter_3_out, shifter_4_out;

  Shifter #(.width(16)) shifter_1 (.in(A), .\dist (SA), .out(shifter_1_out));
  Shifter #(.width(16), .shift("lr")) shifter_2 (.in(A), .\dist (SA), .out(shifter_2_out));
  Shifter #(.width(16), .shift("ar")) shifter_3 (.in(A), .\dist (SA), .out(shifter_3_out));
  Shifter #(.width(16), .shift("rr")) shifter_4 (.in(A), .\dist (SA), .out(shifter_4_out));
  Multiplexer #(.select(2), .width(16), .disabled(0), .enable("false")) multiplexer_1 (
    .in0(shifter_1_out), .in1(shifter_2_out), .in2(shifter_3_out), .in3(shifter_4_out), .out(O), .sel(Sel));
endmodule

module Set_Less_Than_Unit (
  input  OF,
  input  R_sign,
  input  Sign_A,
  input  Sign_B,
  input  SLTU,
  output [15:0] SLT
);

  wire and_1_out, multiplexer_1_out, not_1_out, xor_1_out, xor_2_out;

  xor xor_1 (xor_1_out, OF, R_sign);
  xor xor_2 (xor_2_out, Sign_A, Sign_B);
  and and_1 (and_1_out, xor_1_out, xor_2_out);
  not not_1 (not_1_out, and_1_out);
  Multiplexer #(.disabled(0), .enable("false")) multiplexer_1 (
    .in0(xor_1_out), .in1(not_1_out), .out(multiplexer_1_out), .sel(SLTU));
  assign SLT = {{15{1'b0}}, multiplexer_1_out};  // Bit_Extender bit_extender_1
endmodule

module Load_Upper_Imm (
  input  [10:0] _11_bit_Imm,
  output [15:0] _11_shifted_16
);


  assign _11_shifted_16 = {_11_bit_Imm, {5{1'b0}}};
endmodule
